# Fritzing sketch LM393-prototype (saved by Fritzing 0.9.6b)
perfboards: 1

parts:
  M1 = fc-51 [package=THT]  # not connected
  M2 = fc-51 [package=THT]
  Part1 = Adafruit Motor/Stepper/Servo Shield [part_number="Adafruit #1438"]
  R1 = Resistor [tolerance=±5% power=0.25 resistance=220 package=THT]  # not connected
  R2 = Resistor [tolerance=±5% power=0.25 resistance=220 package=THT]

nets:
  N1: M2.pin3, Part1.+5V
  N2: Part1.GND, R2.Pin_1

custom parts:
  Adafruit Motor/Stepper/Servo Shield: The original Adafruit Motorshield kit is one of our most beloved kits, which is why we decided to make something even better. We have upgraded the shield kit to make the bestest, easiest way to drive DC and Stepper motors. This shield will make quick work of your next robotics project! We kept the ability to drive up to 4 DC motors or 2 stepper motors, but added many improvements: Instead of a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
