# Fritzing sketch Narcissa (saved by Fritzing 0.9.6b)
breadboards: 1

parts:
  Part1 = Adafruit Motor/Stepper/Servo Shield [part_number="Adafruit #1438"]
  Part2 = Arduino Uno (Rev3)  # not connected
  M1 = gear-motor
  M2 = gear-motor
  M3 = gear-motor
  M4 = gear-motor
  Enc1 = shaft encoder
  Enc2 = shaft encoder
  Enc3 = shaft encoder
  Enc4 = shaft encoder
  J1 = Basic Servo

nets:
  N1: Part1.M2A, M3.pin_1
  N2: Part1.M2B, M3.pin_2
  N3: Part1.M1B, M1.pin_1
  N4: Part1.M1A, M1.pin_2
  N5: Part1.M3A, M4.pin_2
  N6: Part1.M3B, M4.pin_1
  N7: Part1.M4B, M2.pin_2
  N8: Part1.M4A, M2.pin_1
  VCC: Part1.+5V, Enc1.VCC, Enc2.VCC, Enc3.VCC, Enc4.VCC, J1.vcc
  GND: Part1.GND, Enc1.GND, Enc2.GND, Enc3.GND, Enc4.GND, J1.gnd
  N9: Part1.D10, J1.pulse

custom parts:
  Adafruit Motor/Stepper/Servo Shield: The original Adafruit Motorshield kit is one of our most beloved kits, which is why we decided to make something even better. We have upgraded the shield kit to make the bestest, easiest way to drive DC and Stepper motors. This shield will make quick work of your next robotics project! We kept the ability to drive up to 4 DC motors or 2 stepper motors, but added many improvements: Instead of a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
